# Fritzing sketch IoT-Temp-Monitor_schematic (saved by Fritzing 1.0.8)

parts:
  Part1 = Arduino Uno (Rev3) - ICSP
  Adafruit_DS2482S-800_8_Channel_I2C_to_1-Wire_Bus_Adapter1 = Adafruit DS2482S-800 8 Channel I2C to 1-Wire Bus Adapter [mn=Adafruit mpn=#6027 part_number=#6027]
  T1 = LM34 Temperature Sensor [package="TO92 [THT]"]
  R1 = Resistor [tolerance=±5% power=0.25W resistance=220 package=THT]
  LED1 = RGB LED (com. cathode, rbg) [color="Red (633nm)" current=0.030A package="5 mm [THT]"]
  Part4 = OLED Monochrome 128x32 I2C [part_number=931]
  J1 = Piezo Speaker

nets:
  N1: Part1.A2, Adafruit_DS2482S-800_8_Channel_I2C_to_1-Wire_Bus_Adapter1.SDA, Part4.SDA
  N2: Part1.A3, Adafruit_DS2482S-800_8_Channel_I2C_to_1-Wire_Bus_Adapter1.SCL, Part4.SCL
  5V: Part1.5V, Adafruit_DS2482S-800_8_Channel_I2C_to_1-Wire_Bus_Adapter1.VCC, T1.+Vs
  N3: Part1.D8, J1.pin2
  N4: Part1.D9_PWM, R1.Pin_1
  GND: Part1.GND, Adafruit_DS2482S-800_8_Channel_I2C_to_1-Wire_Bus_Adapter1.GND, T1.GND, Part4.GND, J1.pin1
  3V3: Part1.3V3, Part4.3.3V
  N5: Adafruit_DS2482S-800_8_Channel_I2C_to_1-Wire_Bus_Adapter1.OW0, T1.Vout
  N6: R1.Pin_0, LED1.red_anode
